// Logisim project circuit1.circ as structural Verilog: 1 circuit, main circuit main
module main (
);

  wire and_1_out, decoder_1_out0, decoder_1_out1, decoder_1_out2, decoder_1_out3, dipswitch_1_sw1,
       dipswitch_1_sw2, xor_1_out;
  wire [1:0] dipswitch_2_sw2;

  DipSwitch #(.number(2)) dipswitch_1 (.sw1(dipswitch_1_sw1), .sw2(dipswitch_1_sw2));
  xor xor_1 (xor_1_out, dipswitch_1_sw1, dipswitch_1_sw2);
  and and_1 (and_1_out, dipswitch_1_sw1, dipswitch_1_sw2);
  LED led_1 (.in(xor_1_out));
  LED led_2 (.in(and_1_out));
  Decoder #(.select(2)) decoder_1 (
    .out0(decoder_1_out0), .out1(decoder_1_out1), .out2(decoder_1_out2), .out3(decoder_1_out3),
    .sel(dipswitch_2_sw2));  // open: en
  DipSwitch #(.number(2)) dipswitch_2 (.sw1(dipswitch_2_sw2[1]), .sw2(dipswitch_2_sw2[0]));
  LED led_3 (.in(decoder_1_out0));
  LED led_4 (.in(decoder_1_out1));
  LED led_5 (.in(decoder_1_out2));
  LED led_6 (.in(decoder_1_out3));
endmodule
